# Fritzing sketch priot_circuit (saved by Fritzing 0.9.3b)

parts:
  A1 = MH-FMD buzzer
  A2 = DHT22 module
  U1 = LuaNode32 / ESP32 [part_number=ESP32S-PIN30]
  Part1 = FC-28 Soil Hygrometer Module - Probe
  Part2 = FC-28 Soil Hygrometer Module
  P1 = S1133 Si Photodiode [package="8mm Ceramic [THT]"]
  Part3 = FC-28 Soil Hygrometer Module
  BAT1 = BC9VPC [package=bc9vpc]

nets:
  VCC: A1.Pin_1, A2.+, U1.3V3, Part2.VCC, Part3.VCC
  N1: A1.Pin_2, U1.D5
  GND: A1.Pin_3, A2.-, U1.GND, Part2.GND, Part3.GND, BAT1.V-
  N2: A2.Out, U1.D4
  N3: U1.D32, Part3.DO
  N4: U1.D33, Part2.AO
  N5: U1.Vin, BAT1.V+
  N6: Part1.POS, Part2.NEG
  N7: Part1.NEG, Part2.POS
  N8: P1.cathode, Part3.NEG
  N9: P1.anode, Part3.POS

custom parts:
  MH-FMD buzzer: MH-FMD buzzer.
  DHT22 module: DHT22 module. Pins VCC Data GND.
  LuaNode32 / ESP32: New Image for LuaNode32 DOIT ESP32 DEVKIT V1. Base parts from LuaNode32 / ESP32 ESP32 based LuaNode32 by G.Noorlander DOIT Esp32 DevKit v1 (30 pins long, 11 pins width) by Werner Rothschopf (modified by vanepp Dec 2018)
  FC-28 Soil Hygrometer Module - Probe: The FC-28 is a soil hygrometer module that uses the Texas Instruments LM393 comparator chip to provide an analog measurement of soil humidity.
  FC-28 Soil Hygrometer Module: The FC-28 is a soil hygrometer module that uses the Texas Instruments LM393 comparator chip to provide an analog measurement of soil humidity. The digital output is high when soil moisture is over a certain threshold, as determined by adjusting the potentiometer.
